// Logisim project mnoznik.circ as structural Verilog: 8 circuits, main circuit rca
module mymul (
  input  [4:0] err_sum1,
  input  [4:0] err_sum2,
  input  [4:0] err_sum3_1,
  input  [4:0] err_sum3,
  input  [4:0] err_sum4_2,
  input  [4:0] err_sum4_1,
  input  [4:0] err_sum4,
  input  [4:0] err_sum5_2,
  input  [4:0] err_sum5_1,
  input  [4:0] err_sum5,
  input  [4:0] err_sum6,
  input  [4:0] err_sum6_2,
  input  [4:0] err_sum7,
  input  [15:0] err_mul,
  input  [3:0] A,
  input  [3:0] B,
  output [7:0] MUL
);

  wire and_1_out, and_2_out, and_3_out, and_4_out, and_5_out, and_6_out, and_7_out, and_8_out, and_9_out,
       and_10_out, and_11_out, and_12_out, and_13_out, and_14_out, and_15_out, and_16_out, rca_1_cout,
       rca_2_cout, rca_3_cout, rca_3_s, rca_4_cout, rca_4_s, rca_5_cout, rca_5_s, rca_6_cout, rca_7_cout,
       rca_7_s, rca_8_cout, rca_8_s, rca_9_cout, rca_9_s, rca_10_cout, rca_11_cout, rca_12_cout, xor_1_out,
       xor_2_out, xor_3_out, xor_4_out, xor_5_out, xor_6_out, xor_7_out, xor_8_out, xor_9_out, xor_10_out,
       xor_11_out, xor_12_out, xor_13_out, xor_14_out, xor_15_out, xor_16_out;

  xor xor_1 (xor_1_out, err_mul[12], and_1_out);
  and and_1 (and_1_out, B[0], A[0]);
  xor xor_2 (xor_2_out, err_mul[13], and_2_out);
  and and_2 (and_2_out, B[0], A[1]);
  xor xor_3 (xor_3_out, err_mul[14], and_3_out);
  and and_3 (and_3_out, B[0], A[2]);
  xor xor_4 (xor_4_out, err_mul[15], and_4_out);
  and and_4 (and_4_out, B[0], A[3]);
  xor xor_5 (xor_5_out, err_mul[8], and_5_out);
  and and_5 (and_5_out, B[1], A[0]);
  xor xor_6 (xor_6_out, err_mul[9], and_6_out);
  and and_6 (and_6_out, B[1], A[1]);
  xor xor_7 (xor_7_out, err_mul[10], and_7_out);
  and and_7 (and_7_out, B[1], A[2]);
  xor xor_8 (xor_8_out, err_mul[11], and_8_out);
  and and_8 (and_8_out, B[1], A[3]);
  and and_9 (and_9_out, B[2], A[0]);
  and and_10 (and_10_out, B[2], A[1]);
  and and_11 (and_11_out, B[2], A[2]);
  and and_12 (and_12_out, B[2], A[3]);
  xor xor_9 (xor_9_out, err_mul[4], and_9_out);
  xor xor_10 (xor_10_out, err_mul[5], and_10_out);
  xor xor_11 (xor_11_out, err_mul[6], and_11_out);
  xor xor_12 (xor_12_out, err_mul[7], and_12_out);
  and and_13 (and_13_out, B[3], A[0]);
  and and_14 (and_14_out, B[3], A[1]);
  and and_15 (and_15_out, B[3], A[2]);
  and and_16 (and_16_out, B[3], A[3]);
  xor xor_13 (xor_13_out, err_mul[0], and_13_out);
  xor xor_14 (xor_14_out, err_mul[1], and_14_out);
  xor xor_15 (xor_15_out, err_mul[2], and_15_out);
  xor xor_16 (xor_16_out, err_mul[3], and_16_out);
  rca rca_1 (.err(err_sum1), .A(xor_1_out), .S(MUL[0]), .Cout(rca_1_cout));  // open: Cin, B
  rca rca_2 (.err(err_sum2), .Cin(rca_1_cout), .A(xor_2_out), .S(MUL[1]), .Cout(rca_2_cout));  // open: B
  rca rca_3 (.err(err_sum3), .Cin(rca_2_cout), .B(xor_6_out), .A(xor_3_out), .S(rca_3_s), .Cout(rca_3_cout));
  rca rca_4 (.err(err_sum4), .Cin(rca_3_cout), .B(xor_7_out), .A(xor_4_out), .S(rca_4_s), .Cout(rca_4_cout));
  rca rca_5 (.err(err_sum5), .Cin(rca_4_cout), .B(xor_8_out), .S(rca_5_s), .Cout(rca_5_cout));  // open: A
  rca rca_6 (.err(err_sum3_1), .B(xor_9_out), .A(rca_3_s), .S(MUL[2]), .Cout(rca_6_cout));  // open: Cin
  rca rca_7 (.err(err_sum4_1), .Cin(rca_6_cout), .B(xor_10_out), .A(rca_4_s), .S(rca_7_s), .Cout(rca_7_cout));
  rca rca_8 (.err(err_sum5_1), .Cin(rca_7_cout), .B(xor_11_out), .A(rca_5_s), .S(rca_8_s), .Cout(rca_8_cout));
  rca rca_9 (.err(err_sum6), .Cin(rca_8_cout), .B(rca_5_cout), .A(xor_15_out), .S(rca_9_s), .Cout(rca_9_cout));
  rca rca_10 (.err(err_sum4_2), .B(xor_13_out), .A(rca_7_s), .S(MUL[3]), .Cout(rca_10_cout));  // open: Cin
  rca rca_11 (.err(err_sum5_2), .Cin(rca_10_cout), .B(xor_14_out), .A(rca_8_s), .S(MUL[4]), .Cout(rca_11_cout));
  rca rca_12 (.err(err_sum6_2), .Cin(rca_11_cout), .A(rca_9_s), .S(MUL[5]), .Cout(rca_12_cout));  // open: B
  rca rca_13 (.err(err_sum7), .Cin(rca_12_cout), .B(xor_16_out), .A(rca_9_cout), .S(MUL[6]), .Cout(MUL[7]));
endmodule

module rca (
  input  [4:0] err,
  input  Cin,
  input  B,
  input  A,
  output S,
  output Cout
);

  wire and_1_out, and_2_out, e3_out, or_1_out, or_2_out, xor_1_out, xor_2_out, xor_4_out;

  xor xor_1 (xor_1_out, B, A);
  and and_1 (and_1_out, B, A);
  or or_1 (or_1_out, xor_1_out, err[3]);
  xor xor_2 (xor_2_out, and_1_out, err[4]);
  xor e3 (e3_out, Cin, or_1_out);
  and and_2 (and_2_out, or_1_out, Cin);
  xor xor_3 (S, err[1], e3_out);
  xor xor_4 (xor_4_out, err[2], and_2_out);
  or or_2 (or_2_out, xor_4_out, xor_2_out);
  xor xor_5 (Cout, err[0], or_2_out);
endmodule

module bit4mod3 (
  input  [3:0] x,
  output [1:0] y
);

  wire and_1_out, and_2_out, and_3_out, and_4_out, and_5_out, and_6_out, and_7_out, and_8_out, not_1_out,
       not_2_out, not_3_out, not_4_out;

  not not_1 (not_1_out, x[3]);
  not not_2 (not_2_out, x[2]);
  not not_3 (not_3_out, x[1]);
  not not_4 (not_4_out, x[0]);
  and and_1 (and_1_out, not_1_out, not_2_out, x[1], not_4_out);
  and and_2 (and_2_out, not_1_out, x[2], x[0]);
  and and_3 (and_3_out, x[3], not_2_out, not_3_out, not_4_out);
  and and_4 (and_4_out, x[3], not_2_out, x[1], x[0]);
  and and_5 (and_5_out, x[3], x[2], x[1], not_4_out);
  and and_6 (and_6_out, not_1_out, not_2_out, not_3_out, x[0]);
  and and_7 (and_7_out, x[2], not_4_out);
  or or_1 (y[0], and_6_out, and_7_out, and_8_out);
  and and_8 (and_8_out, x[3], not_4_out);
  or or_2 (y[1], and_1_out, and_2_out, and_3_out, and_4_out, and_5_out);
endmodule

module main (
  input  in_1,
  input  in_2,
  input  in_3,
  input  in_4,
  input  in_5,
  input  in_6,
  input  in_7,
  input  in_8,
  input  in_9,
  input  in_10,
  input  in_11,
  input  in_12,
  input  in_13,
  input  in_14,
  input  in_15,
  input  in_16,
  input  in_17,
  input  in_18,
  input  in_19,
  input  [3:0] a,
  input  in_21,
  input  [3:0] b,
  input  in_23,
  input  in_24,
  input  in_25,
  input  in_26,
  input  in_27,
  input  in_28,
  input  in_29,
  input  in_30,
  input  in_31,
  input  in_32,
  input  in_33,
  input  in_34,
  input  in_35,
  input  in_36,
  input  in_37,
  input  in_38,
  input  in_39,
  input  in_40,
  input  in_41,
  input  in_42,
  input  in_43,
  input  in_44,
  input  in_45,
  input  in_46,
  input  in_47,
  input  in_48,
  input  in_49,
  input  in_50,
  input  in_51,
  input  in_52,
  input  in_53,
  input  in_54,
  input  in_55,
  input  in_56,
  input  in_57,
  input  in_58,
  input  in_59,
  input  in_60,
  input  in_61,
  input  in_62,
  input  in_63,
  input  in_64,
  input  in_65,
  input  in_66,
  input  in_67,
  input  in_68,
  input  in_69,
  input  in_70,
  input  in_71,
  input  in_72,
  input  in_73,
  input  in_74,
  input  in_75,
  input  in_76,
  input  in_77,
  input  in_78,
  input  in_79,
  input  in_80,
  input  in_81,
  input  in_82,
  input  in_83,
  input  in_84,
  input  in_85,
  input  in_86,
  input  in_87,
  input  in_88,
  input  in_89,
  input  in_90,
  input  in_91,
  input  in_92,
  input  in_93,
  input  in_94,
  input  in_95,
  input  in_96,
  input  in_97,
  input  in_98,
  input  in_99,
  input  in_100,
  input  in_101,
  input  in_102,
  input  in_103,
  input  in_104,
  input  in_105,
  input  in_106,
  input  in_107,
  output [7:0] mul,
  output [1:0] out_109,
  output [1:0] out_110,
  output err
);

  wire thesame2x2_1_ok;
  wire [1:0] bit4mod3_1_y, bit4mod3_2_y;
  wire [3:0] mymul2_1_p8;

  // mymul mymul_1: pin names not known; wires that end beside it: in_1, in_2, in_3, in_4, in_5, in_6, in_7, in_8, in_9, in_10, in_11, in_12, in_13, in_14, in_15, in_16, in_17, mul
  bit4mod3 bit4mod3_1 (.x(a), .y(bit4mod3_1_y));
  bit4mod3 bit4mod3_2 (.x(b), .y(bit4mod3_2_y));
  fixed8mod3 fixed8mod3_1 (.x(mul), .y(out_109));
  // mymul2 mymul2_1: pin names not known; wires that end beside it: in_25, in_27, in_29, in_31, in_33, in_35, in_37, mymul2_1_p8
  bit4mod3 bit4mod3_3 (.x(mymul2_1_p8), .y(out_110));
  not not_1 (err, thesame2x2_1_ok);
  thesame2x2 thesame2x2_1 (.a(out_109), .b(out_110), .ok(thesame2x2_1_ok));
endmodule

module better8mod3 (
  input  [7:0] x,
  output [1:0] y
);

  wire and_1_out, and_2_out, and_3_out, not_1_out, not_2_out, not_3_out, not_4_out, not_5_out, not_6_out,
       not_7_out, not_8_out, or_1_out, or_2_out, or_3_out, or_4_out, or_5_out, or_6_out, or_7_out, or_8_out,
       or_9_out, or_10_out, or_11_out, or_12_out, or_13_out, or_14_out, or_15_out, or_16_out, or_17_out,
       or_18_out, or_19_out, or_20_out, or_21_out, or_22_out, or_23_out, or_24_out, or_25_out, or_26_out,
       or_27_out, or_28_out, or_29_out, or_30_out, or_31_out, or_32_out, or_33_out, or_34_out, or_35_out,
       or_36_out, or_37_out, or_38_out, or_39_out, or_40_out, or_41_out, or_42_out, or_43_out, or_44_out,
       or_45_out, or_46_out, or_47_out, or_48_out, or_49_out, or_50_out, or_51_out, or_52_out, or_53_out,
       or_54_out, or_55_out, or_56_out, or_57_out, or_58_out, or_59_out, or_60_out, or_61_out, or_62_out,
       or_63_out, or_64_out, or_65_out, or_66_out, or_67_out, or_68_out, or_69_out, or_70_out, or_71_out,
       or_72_out, or_73_out, or_74_out, or_75_out, or_76_out, or_77_out, or_78_out, or_79_out, or_80_out,
       or_81_out, or_82_out, or_83_out, or_84_out, or_85_out, or_86_out, or_87_out, or_88_out, or_89_out,
       or_90_out, or_91_out, or_92_out, or_93_out, or_94_out, or_95_out, or_96_out, or_97_out, or_98_out,
       or_99_out, or_100_out, or_101_out, or_102_out, or_103_out, or_104_out, or_105_out, or_106_out,
       or_107_out, or_108_out, or_109_out, or_110_out, or_111_out, or_112_out, or_113_out, or_114_out,
       or_115_out, or_116_out, or_117_out, or_118_out, or_119_out, or_120_out, or_121_out, or_122_out,
       or_123_out, or_124_out, or_125_out, or_126_out, or_127_out, or_128_out, or_129_out, or_130_out,
       or_131_out, or_132_out, or_133_out, or_134_out, or_135_out, or_136_out, or_137_out, or_138_out,
       or_139_out, or_140_out, or_141_out, or_142_out, or_143_out, or_144_out, or_145_out, or_146_out,
       or_147_out, or_148_out, or_149_out, or_150_out, or_151_out, or_152_out, or_153_out, or_154_out,
       or_155_out, or_156_out, or_157_out, or_158_out, or_159_out, or_160_out, or_161_out, or_162_out,
       or_163_out, or_164_out, or_165_out, or_166_out;

  not not_1 (not_1_out, x[7]);
  not not_2 (not_2_out, x[6]);
  not not_3 (not_3_out, x[5]);
  not not_4 (not_4_out, x[4]);
  not not_5 (not_5_out, x[3]);
  not not_6 (not_6_out, x[2]);
  not not_7 (not_7_out, x[1]);
  not not_8 (not_8_out, x[0]);
  or or_1 (or_1_out, x[7], x[5], not_4_out, x[3], not_6_out, x[1], not_8_out);
  or or_2 (or_2_out, x[7], not_2_out, x[5], x[3], not_6_out, x[1], not_8_out);
  or or_3 (or_3_out, x[7], not_2_out, x[5], not_4_out, x[3], x[1], not_8_out);
  or or_4 (or_4_out, x[7], not_2_out, x[5], not_4_out, x[3], not_6_out, x[1]);
  or or_5 (or_5_out, x[7], not_2_out, x[5], not_4_out, x[3], not_6_out, not_8_out);
  or or_6 (or_6_out, x[7], not_2_out, x[5], not_4_out, not_6_out, x[1], not_8_out);
  or or_7 (or_7_out, x[7], not_2_out, not_4_out, x[3], not_6_out, x[1], not_8_out);
  or or_8 (or_8_out, not_2_out, x[5], not_4_out, x[3], not_6_out, x[1], not_8_out);
  or or_9 (or_9_out, x[7], x[6], x[5], x[4], x[3], x[2], x[1]);
  or or_10 (or_10_out, x[7], x[6], x[5], x[4], x[3], x[2], not_8_out);
  or or_11 (or_11_out, x[7], x[6], x[5], x[4], x[3], x[1], x[0]);
  or or_12 (or_12_out, x[7], x[6], x[5], x[4], x[3], not_6_out, x[0]);
  or or_13 (or_13_out, x[7], x[6], x[5], x[4], x[3], not_7_out, not_8_out);
  or or_14 (or_14_out, x[7], x[6], x[5], x[4], x[2], x[1], not_8_out);
  or or_15 (or_15_out, x[7], x[6], x[4], not_5_out, x[2], not_7_out, x[0]);
  or or_16 (or_16_out, x[7], x[6], x[5], x[4], not_6_out, x[1], x[0]);
  or or_17 (or_17_out, x[7], x[6], x[5], x[4], not_5_out, x[1], not_8_out);
  or or_18 (or_18_out, x[7], x[6], x[5], x[4], not_6_out, not_7_out, not_8_out);
  or or_19 (or_19_out, x[7], x[6], x[5], x[3], x[2], x[1], x[0]);
  or or_20 (or_20_out, x[7], x[6], x[5], not_4_out, x[3], x[2], x[0]);
  or or_21 (or_21_out, x[7], x[6], x[5], x[3], x[2], not_7_out, not_8_out);
  or or_22 (or_22_out, x[7], x[6], x[5], x[3], not_6_out, not_7_out, x[0]);
  or or_23 (or_23_out, x[7], x[6], x[5], not_4_out, x[2], x[1], x[0]);
  or or_24 (or_24_out, x[7], x[6], x[5], not_5_out, x[2], x[1], not_8_out);
  or or_25 (or_25_out, x[7], x[6], x[5], not_4_out, x[2], not_7_out, not_8_out);
  or or_26 (or_26_out, x[7], x[6], x[5], not_5_out, not_6_out, x[1], x[0]);
  or or_27 (or_27_out, x[7], x[6], x[5], not_4_out, not_6_out, not_7_out, x[0]);
  or or_28 (or_28_out, x[7], x[6], x[5], not_5_out, not_6_out, not_7_out, not_8_out);
  or or_29 (or_29_out, x[7], x[6], x[4], x[3], x[2], x[1], not_8_out);
  or or_30 (or_30_out, x[7], x[6], not_3_out, x[4], x[2], not_7_out, x[0]);
  or or_31 (or_31_out, x[7], x[6], x[4], x[3], not_6_out, x[1], x[0]);
  or or_32 (or_32_out, x[7], x[6], not_3_out, x[4], x[3], x[1], not_8_out);
  or or_33 (or_33_out, x[7], x[6], x[4], x[3], not_6_out, not_7_out, not_8_out);
  or or_34 (or_34_out, x[7], x[6], not_3_out, x[4], not_5_out, x[2], x[0]);
  or or_35 (or_35_out, x[7], x[6], not_3_out, x[4], not_5_out, x[2], not_7_out);
  or or_36 (or_36_out, x[7], x[6], x[4], not_5_out, not_6_out, x[1], not_8_out);
  or or_37 (or_37_out, x[7], x[6], not_3_out, x[4], not_5_out, not_7_out, x[0]);
  or or_38 (or_38_out, x[7], x[6], not_4_out, x[3], x[2], x[1], x[0]);
  or or_39 (or_39_out, x[7], x[6], not_3_out, x[3], x[2], x[1], not_8_out);
  or or_40 (or_40_out, x[7], x[6], not_4_out, x[3], x[2], not_7_out, not_8_out);
  or or_41 (or_41_out, x[7], x[6], not_3_out, x[3], not_6_out, x[1], x[0]);
  or or_42 (or_42_out, x[7], x[6], not_4_out, x[3], not_6_out, not_7_out, x[0]);
  or or_43 (or_43_out, x[7], x[6], not_3_out, x[3], not_6_out, not_7_out, not_8_out);
  or or_44 (or_44_out, x[7], x[6], not_4_out, not_5_out, x[2], x[1], not_8_out);
  or or_45 (or_45_out, x[7], x[6], not_3_out, not_5_out, x[2], not_7_out, x[0]);
  or or_46 (or_46_out, x[7], x[6], not_4_out, not_5_out, not_6_out, x[1], x[0]);
  or or_47 (or_47_out, x[7], x[6], not_3_out, not_5_out, not_6_out, x[1], not_8_out);
  or or_48 (or_48_out, x[7], x[6], not_4_out, not_5_out, not_6_out, not_7_out, not_8_out);
  or or_49 (or_49_out, x[7], x[5], x[4], x[3], x[2], x[1], x[0]);
  or or_50 (or_50_out, x[7], not_2_out, x[5], x[4], x[3], x[2], x[0]);
  or or_51 (or_51_out, x[7], not_2_out, x[5], x[4], x[3], x[2], not_7_out);
  or or_52 (or_52_out, x[7], not_2_out, x[5], x[4], x[3], not_7_out, x[0]);
  or or_53 (or_53_out, x[7], not_2_out, x[5], x[4], x[2], x[1], x[0]);
  or or_54 (or_54_out, x[7], not_2_out, x[5], x[4], not_5_out, x[2], x[1]);
  or or_55 (or_55_out, x[7], not_2_out, x[5], x[4], x[2], not_7_out, not_8_out);
  or or_56 (or_56_out, x[7], not_2_out, x[5], x[4], not_5_out, x[1], x[0]);
  or or_57 (or_57_out, x[7], not_2_out, x[5], x[4], not_6_out, not_7_out, x[0]);
  or or_58 (or_58_out, x[7], x[5], x[4], not_5_out, not_6_out, not_7_out, not_8_out);
  or or_59 (or_59_out, x[7], not_2_out, x[5], x[3], x[2], not_7_out, x[0]);
  or or_60 (or_60_out, x[7], not_2_out, x[5], not_5_out, x[2], x[1], x[0]);
  or or_61 (or_61_out, x[7], not_2_out, x[5], not_4_out, x[2], not_7_out, x[0]);
  or or_62 (or_62_out, x[7], x[5], not_4_out, not_5_out, x[2], not_7_out, not_8_out);
  or or_63 (or_63_out, x[7], x[5], not_4_out, not_5_out, not_6_out, not_7_out, x[0]);
  or or_64 (or_64_out, x[7], not_2_out, x[4], x[3], x[2], x[1], x[0]);
  or or_65 (or_65_out, x[7], not_2_out, not_3_out, x[4], x[3], x[2], x[1]);
  or or_66 (or_66_out, x[7], not_2_out, x[4], x[3], x[2], not_7_out, not_8_out);
  or or_67 (or_67_out, x[7], not_2_out, not_3_out, x[4], x[3], x[1], x[0]);
  or or_68 (or_68_out, x[7], not_2_out, x[4], x[3], not_6_out, not_7_out, x[0]);
  or or_69 (or_69_out, x[7], not_3_out, x[4], x[3], not_6_out, not_7_out, not_8_out);
  or or_70 (or_70_out, x[7], not_2_out, x[4], not_5_out, x[2], x[1], not_8_out);
  or or_71 (or_71_out, x[7], not_3_out, x[4], not_5_out, x[2], not_7_out, x[0]);
  or or_72 (or_72_out, x[7], not_2_out, x[4], not_5_out, not_6_out, x[1], x[0]);
  or or_73 (or_73_out, x[7], not_3_out, x[4], not_5_out, not_6_out, x[1], not_8_out);
  or or_74 (or_74_out, x[7], not_2_out, x[4], not_5_out, not_6_out, not_7_out, not_8_out);
  or or_75 (or_75_out, x[7], not_2_out, not_3_out, x[3], x[2], x[1], x[0]);
  or or_76 (or_76_out, x[7], not_2_out, not_4_out, x[3], x[2], not_7_out, x[0]);
  or or_77 (or_77_out, x[7], not_3_out, not_4_out, x[3], x[2], not_7_out, not_8_out);
  or or_78 (or_78_out, x[7], not_3_out, not_4_out, x[3], not_6_out, not_7_out, x[0]);
  or or_79 (or_79_out, x[7], not_2_out, not_4_out, not_5_out, x[2], x[1], x[0]);
  or or_80 (or_80_out, x[7], not_3_out, not_4_out, not_5_out, x[2], x[1], not_8_out);
  or or_81 (or_81_out, x[7], not_2_out, not_4_out, not_5_out, x[2], not_7_out, not_8_out);
  or or_82 (or_82_out, x[7], not_3_out, not_4_out, not_5_out, not_6_out, x[1], x[0]);
  or or_83 (or_83_out, x[7], not_2_out, not_4_out, not_5_out, not_6_out, not_7_out, x[0]);
  or or_84 (or_84_out, x[7], not_2_out, not_3_out, not_5_out, not_6_out, not_7_out, not_8_out);
  or or_85 (or_85_out, x[6], x[5], x[4], x[3], x[2], x[1], not_8_out);
  or or_86 (or_86_out, not_1_out, x[6], x[5], x[4], x[2], not_7_out, x[0]);
  or or_87 (or_87_out, x[6], x[5], x[4], x[3], not_6_out, x[1], x[0]);
  or or_88 (or_88_out, not_1_out, x[6], x[5], x[4], x[3], x[1], not_8_out);
  or or_89 (or_89_out, not_1_out, x[6], x[5], x[4], x[3], not_6_out, not_8_out);
  or or_90 (or_90_out, not_1_out, x[6], x[5], x[4], not_5_out, x[2], x[0]);
  or or_91 (or_91_out, not_1_out, x[6], x[5], x[4], not_5_out, x[2], not_7_out);
  or or_92 (or_92_out, not_1_out, x[6], x[5], x[4], not_6_out, x[1], not_8_out);
  or or_93 (or_93_out, not_1_out, x[6], x[5], x[4], not_5_out, not_7_out, x[0]);
  or or_94 (or_94_out, x[6], x[5], not_4_out, x[3], x[2], x[1], x[0]);
  or or_95 (or_95_out, not_1_out, x[6], x[5], x[3], x[2], x[1], not_8_out);
  or or_96 (or_96_out, not_1_out, x[6], x[5], not_4_out, x[3], x[2], not_8_out);
  or or_97 (or_97_out, not_1_out, x[6], x[5], x[3], not_6_out, x[1], x[0]);
  or or_98 (or_98_out, not_1_out, x[6], x[5], not_4_out, x[3], not_6_out, x[0]);
  or or_99 (or_99_out, not_1_out, x[6], x[5], x[3], not_6_out, not_7_out, not_8_out);
  or or_100 (or_100_out, not_1_out, x[6], x[5], not_4_out, x[2], x[1], not_8_out);
  or or_101 (or_101_out, not_1_out, x[6], x[5], not_5_out, x[2], not_7_out, x[0]);
  or or_102 (or_102_out, not_1_out, x[6], x[5], not_4_out, not_6_out, x[1], x[0]);
  or or_103 (or_103_out, not_1_out, x[6], x[5], not_5_out, not_6_out, x[1], not_8_out);
  or or_104 (or_104_out, not_1_out, x[6], x[5], not_4_out, not_6_out, not_7_out, not_8_out);
  or or_105 (or_105_out, not_1_out, x[6], not_3_out, x[4], x[3], x[2], x[0]);
  or or_106 (or_106_out, not_1_out, x[6], not_3_out, x[4], x[3], x[2], not_7_out);
  or or_107 (or_107_out, not_1_out, x[6], x[4], x[3], not_6_out, x[1], not_8_out);
  or or_108 (or_108_out, not_1_out, x[6], not_3_out, x[4], x[3], not_7_out, x[0]);
  or or_109 (or_109_out, not_1_out, x[6], not_3_out, x[4], x[2], x[1], x[0]);
  or or_110 (or_110_out, not_1_out, x[6], not_3_out, x[4], not_5_out, x[2], x[1]);
  or or_111 (or_111_out, not_1_out, x[6], x[4], not_5_out, x[2], not_7_out, not_8_out);
  or or_112 (or_112_out, not_1_out, x[6], not_3_out, x[4], not_5_out, x[1], x[0]);
  or or_113 (or_113_out, not_1_out, x[6], x[4], not_5_out, not_6_out, not_7_out, x[0]);
  or or_114 (or_114_out, not_1_out, x[6], not_3_out, x[4], not_5_out, not_7_out, not_8_out);
  or or_115 (or_115_out, not_1_out, x[6], not_4_out, x[3], x[2], x[1], not_8_out);
  or or_116 (or_116_out, not_1_out, x[6], not_3_out, x[3], x[2], not_7_out, x[0]);
  or or_117 (or_117_out, not_1_out, x[6], not_4_out, x[3], not_6_out, x[1], x[0]);
  or or_118 (or_118_out, not_1_out, x[6], not_3_out, x[3], not_6_out, x[1], not_8_out);
  or or_119 (or_119_out, not_1_out, x[6], not_4_out, x[3], not_6_out, not_7_out, not_8_out);
  or or_120 (or_120_out, not_1_out, x[6], not_3_out, not_5_out, x[2], x[1], x[0]);
  or or_121 (or_121_out, not_1_out, x[6], not_4_out, not_5_out, x[2], not_7_out, x[0]);
  or or_122 (or_122_out, not_1_out, x[6], not_3_out, not_5_out, x[2], not_7_out, not_8_out);
  or or_123 (or_123_out, not_1_out, x[6], not_4_out, not_5_out, not_6_out, x[1], not_8_out);
  or or_124 (or_124_out, not_1_out, x[6], not_3_out, not_5_out, not_6_out, not_7_out, x[0]);
  or or_125 (or_125_out, not_2_out, x[5], x[4], x[3], x[2], x[1], x[0]);
  or or_126 (or_126_out, not_1_out, not_2_out, x[5], x[4], x[3], x[2], x[1]);
  or or_127 (or_127_out, not_1_out, not_2_out, x[5], x[4], x[3], x[2], not_8_out);
  or or_128 (or_128_out, not_1_out, not_2_out, x[5], x[4], x[3], x[1], x[0]);
  or or_129 (or_129_out, not_1_out, not_2_out, x[5], x[4], x[3], not_6_out, x[0]);
  or or_130 (or_130_out, not_1_out, x[5], x[4], x[3], not_6_out, not_7_out, not_8_out);
  or or_131 (or_131_out, not_1_out, not_2_out, x[5], x[4], x[2], x[1], not_8_out);
  or or_132 (or_132_out, not_1_out, x[5], x[4], not_5_out, x[2], not_7_out, x[0]);
  or or_133 (or_133_out, not_1_out, not_2_out, x[5], x[4], not_6_out, x[1], x[0]);
  or or_134 (or_134_out, not_1_out, x[5], x[4], not_5_out, not_6_out, x[1], not_8_out);
  or or_135 (or_135_out, not_1_out, not_2_out, x[5], x[4], not_6_out, not_7_out, not_8_out);
  or or_136 (or_136_out, not_1_out, not_2_out, x[5], x[3], x[2], x[1], x[0]);
  or or_137 (or_137_out, not_1_out, not_2_out, x[5], not_4_out, x[3], x[2], x[0]);
  or or_138 (or_138_out, not_1_out, x[5], not_4_out, x[3], x[2], not_7_out, not_8_out);
  or or_139 (or_139_out, not_1_out, x[5], not_4_out, x[3], not_6_out, not_7_out, x[0]);
  or or_140 (or_140_out, not_1_out, not_2_out, x[5], not_4_out, x[2], x[1], x[0]);
  or or_141 (or_141_out, not_1_out, x[5], not_4_out, not_5_out, x[2], x[1], not_8_out);
  or or_142 (or_142_out, not_1_out, not_2_out, x[5], not_4_out, x[2], not_7_out, not_8_out);
  or or_143 (or_143_out, not_1_out, x[5], not_4_out, not_5_out, not_6_out, x[1], x[0]);
  or or_144 (or_144_out, not_1_out, not_2_out, x[5], not_4_out, not_6_out, not_7_out, x[0]);
  or or_145 (or_145_out, not_1_out, not_2_out, x[5], not_5_out, not_6_out, not_7_out, not_8_out);
  or or_146 (or_146_out, not_1_out, not_2_out, x[4], x[3], x[2], x[1], not_8_out);
  or or_147 (or_147_out, not_1_out, not_3_out, x[4], x[3], x[2], not_7_out, x[0]);
  or or_148 (or_148_out, not_1_out, not_2_out, x[4], x[3], not_6_out, x[1], x[0]);
  or or_149 (or_149_out, not_1_out, not_3_out, x[4], x[3], not_6_out, x[1], not_8_out);
  or or_150 (or_150_out, not_1_out, not_2_out, x[4], x[3], not_6_out, not_7_out, not_8_out);
  or or_151 (or_151_out, not_1_out, not_3_out, x[4], not_5_out, x[2], x[1], x[0]);
  or or_152 (or_152_out, not_1_out, not_2_out, x[4], not_5_out, x[2], not_7_out, x[0]);
  or or_153 (or_153_out, not_1_out, not_2_out, not_3_out, x[4], not_5_out, x[2], not_7_out);
  or or_154 (or_154_out, not_1_out, not_2_out, x[4], not_5_out, not_6_out, x[1], not_8_out);
  or or_155 (or_155_out, not_1_out, not_2_out, not_3_out, x[4], not_5_out, not_7_out, x[0]);
  or or_156 (or_156_out, not_1_out, not_2_out, not_4_out, x[3], x[2], x[1], x[0]);
  or or_157 (or_157_out, not_1_out, not_3_out, not_4_out, x[3], x[2], x[1], not_8_out);
  or or_158 (or_158_out, not_1_out, not_2_out, not_4_out, x[3], x[2], not_7_out, not_8_out);
  or or_159 (or_159_out, not_1_out, not_3_out, not_4_out, x[3], not_6_out, x[1], x[0]);
  or or_160 (or_160_out, not_1_out, not_2_out, not_4_out, x[3], not_6_out, not_7_out, x[0]);
  or or_161 (or_161_out, not_1_out, not_2_out, not_3_out, x[3], not_6_out, not_7_out, not_8_out);
  or or_162 (or_162_out, not_1_out, not_2_out, not_4_out, not_5_out, x[2], x[1], not_8_out);
  or or_163 (or_163_out, not_1_out, not_2_out, not_3_out, not_5_out, x[2], not_7_out, x[0]);
  or or_164 (or_164_out, not_1_out, not_2_out, not_4_out, not_5_out, not_6_out, x[1], x[0]);
  or or_165 (or_165_out, not_1_out, not_2_out, not_3_out, not_5_out, not_6_out, x[1], not_8_out);
  or or_166 (or_166_out, not_1_out, not_2_out, not_3_out, not_4_out, not_6_out, not_7_out, not_8_out);
  and and_1 (and_1_out, or_1_out, or_2_out, or_3_out, or_4_out, or_5_out, or_6_out, or_7_out, or_8_out, or_9_out, or_10_out, or_11_out, or_12_out, or_13_out, or_14_out, or_15_out, or_16_out, or_17_out, or_18_out, or_19_out, or_20_out, or_21_out, or_22_out, or_23_out, or_24_out, or_25_out, or_26_out, or_27_out, or_28_out, or_29_out, or_30_out, or_31_out, or_32_out, or_33_out, or_34_out, or_35_out, or_36_out, or_37_out, or_38_out, or_39_out, or_40_out, or_41_out, or_42_out, or_43_out, or_44_out, or_45_out, or_46_out, or_47_out, or_48_out, or_49_out, or_50_out, or_51_out, or_52_out, or_53_out, or_54_out, or_55_out, or_56_out);
  and and_2 (and_2_out, or_57_out, or_58_out, or_59_out, or_60_out, or_61_out, or_62_out, or_63_out, or_64_out, or_65_out, or_66_out, or_67_out, or_68_out, or_69_out, or_70_out, or_71_out, or_72_out, or_73_out, or_74_out, or_75_out, or_76_out, or_77_out, or_78_out, or_79_out, or_80_out, or_81_out, or_82_out, or_83_out, or_84_out, or_85_out, or_86_out, or_87_out, or_88_out, or_89_out, or_90_out, or_91_out, or_92_out, or_93_out, or_94_out, or_95_out, or_96_out, or_97_out, or_98_out, or_99_out, or_100_out, or_101_out, or_102_out, or_103_out, or_104_out, or_105_out, or_106_out, or_107_out, or_108_out, or_109_out, or_110_out, or_111_out);
  and and_3 (and_3_out, or_112_out, or_113_out, or_114_out, or_115_out, or_116_out, or_117_out, or_118_out, or_119_out, or_120_out, or_121_out, or_122_out, or_123_out, or_124_out, or_125_out, or_126_out, or_127_out, or_128_out, or_129_out, or_130_out, or_131_out, or_132_out, or_133_out, or_134_out, or_135_out, or_136_out, or_137_out, or_138_out, or_139_out, or_140_out, or_141_out, or_142_out, or_143_out, or_144_out, or_145_out, or_146_out, or_147_out, or_148_out, or_149_out, or_150_out, or_151_out, or_152_out, or_153_out, or_154_out, or_155_out, or_156_out, or_157_out, or_158_out, or_159_out, or_160_out, or_161_out, or_162_out, or_163_out, or_164_out, or_165_out, or_166_out);
  and and_4 (y[1], and_1_out, and_2_out, and_3_out);

  assign y[0] = x[0];
endmodule

module mymul2 (
  input  [4:0] err_sum1,
  input  [4:0] err_sum2,
  input  [4:0] err_sum3,
  input  [3:0] err_mul,
  input  [1:0] A,
  input  [1:0] B,
  output [3:0] MUL
);

  wire and_1_out, and_2_out, and_3_out, and_4_out, b0_cout, b1_cout, xor_1_out, xor_2_out, xor_3_out,
       xor_4_out;

  and and_1 (and_1_out, B[0], A[0]);
  and and_2 (and_2_out, B[0], A[1]);
  xor xor_1 (xor_1_out, err_mul[2], and_1_out);
  xor xor_2 (xor_2_out, err_mul[3], and_2_out);
  and and_3 (and_3_out, B[1], A[0]);
  and and_4 (and_4_out, B[1], A[1]);
  xor xor_3 (xor_3_out, err_mul[0], and_3_out);
  xor xor_4 (xor_4_out, err_mul[1], and_4_out);
  rca b0 (.err(err_sum1), .A(xor_1_out), .S(MUL[0]), .Cout(b0_cout));  // open: Cin, B
  rca b1 (.err(err_sum2), .Cin(b0_cout), .B(xor_3_out), .A(xor_2_out), .S(MUL[1]), .Cout(b1_cout));
  rca rca_1 (.err(err_sum3), .Cin(b1_cout), .B(xor_4_out), .S(MUL[2]), .Cout(MUL[3]));  // open: A
endmodule

module fixed8mod3 (
  input  [7:0] x,
  output [1:0] y
);

  wire and_1_out, and_2_out, and_3_out, and_4_out, and_5_out, and_6_out, and_7_out, and_8_out, and_9_out,
       and_10_out, and_11_out, and_12_out, and_13_out, and_14_out, and_15_out, and_16_out, and_17_out,
       and_18_out, and_19_out, and_20_out, and_21_out, and_22_out, and_23_out, and_24_out, and_25_out,
       and_26_out, and_27_out, and_28_out, and_29_out, and_30_out, and_31_out, and_32_out, and_33_out,
       and_34_out, and_35_out, and_36_out, and_37_out, and_38_out, and_39_out, and_40_out, and_41_out,
       and_42_out, and_43_out, and_44_out, and_45_out, and_46_out, and_47_out, and_48_out, and_49_out,
       and_50_out, and_51_out, and_52_out, and_53_out, and_54_out, and_55_out, and_56_out, and_57_out,
       and_58_out, and_59_out, and_60_out, and_61_out, and_62_out, and_63_out, and_64_out, and_65_out,
       and_66_out, and_67_out, and_68_out, and_69_out, and_70_out, and_71_out, and_72_out, and_73_out,
       and_74_out, and_75_out, and_76_out, and_77_out, and_78_out, and_79_out, and_80_out, and_81_out,
       and_82_out, and_83_out, and_84_out, and_85_out, and_86_out, and_87_out, and_88_out, and_89_out,
       and_90_out, and_91_out, and_92_out, and_93_out, and_94_out, and_95_out, and_96_out, and_97_out,
       and_98_out, and_99_out, and_100_out, and_101_out, and_102_out, and_103_out, and_104_out, and_105_out,
       and_106_out, and_107_out, and_108_out, and_109_out, and_110_out, and_111_out, and_112_out,
       and_113_out, and_114_out, and_115_out, and_116_out, and_117_out, and_118_out, and_119_out,
       and_120_out, and_121_out, and_122_out, and_123_out, and_124_out, and_125_out, and_126_out,
       and_127_out, and_128_out, and_129_out, and_130_out, and_131_out, and_132_out, and_133_out,
       and_134_out, and_135_out, and_136_out, and_137_out, and_138_out, and_139_out, and_140_out,
       and_141_out, and_142_out, and_143_out, and_144_out, and_145_out, and_146_out, and_147_out,
       and_148_out, and_149_out, and_150_out, and_151_out, and_152_out, and_153_out, and_154_out,
       and_155_out, and_156_out, and_157_out, and_158_out, and_159_out, and_160_out, and_161_out,
       and_162_out, and_163_out, and_164_out, and_165_out, and_166_out, and_167_out, and_168_out,
       and_169_out, and_170_out, not_1_out, not_2_out, not_3_out, not_4_out, not_5_out, not_6_out, not_7_out,
       not_8_out, or_1_out, or_2_out, or_3_out, or_4_out;

  not not_1 (not_1_out, x[7]);
  not not_2 (not_2_out, x[6]);
  not not_3 (not_3_out, x[5]);
  not not_4 (not_4_out, x[4]);
  not not_5 (not_5_out, x[3]);
  not not_6 (not_6_out, x[2]);
  not not_7 (not_7_out, x[1]);
  not not_8 (not_8_out, x[0]);
  and and_1 (and_1_out, x[7], not_2_out, not_3_out, not_4_out, not_5_out, not_6_out, not_7_out, not_8_out);
  and and_2 (and_2_out, not_1_out, not_2_out, not_3_out, not_4_out, not_5_out, not_6_out, x[1], not_8_out);
  and and_3 (and_3_out, x[7], not_2_out, not_3_out, not_4_out, not_5_out, not_6_out, x[1], x[0]);
  and and_4 (and_4_out, not_1_out, not_2_out, not_3_out, not_4_out, not_5_out, x[2], not_7_out, x[0]);
  and and_5 (and_5_out, x[7], not_2_out, not_3_out, not_4_out, not_5_out, x[2], x[1], not_8_out);
  and and_6 (and_6_out, not_1_out, not_2_out, not_3_out, not_4_out, x[3], not_6_out, not_7_out, not_8_out);
  and and_7 (and_7_out, x[7], not_2_out, not_3_out, not_4_out, x[3], not_6_out, not_7_out, x[0]);
  and and_8 (and_8_out, not_1_out, not_2_out, not_3_out, not_4_out, x[3], not_6_out, x[1], x[0]);
  and and_9 (and_9_out, x[7], not_2_out, not_3_out, not_4_out, x[3], x[2], not_7_out, not_8_out);
  and and_10 (and_10_out, not_1_out, not_2_out, not_3_out, not_4_out, x[3], x[2], x[1], not_8_out);
  and and_11 (and_11_out, x[7], not_2_out, not_3_out, not_4_out, x[3], x[2], x[1], x[0]);
  and and_12 (and_12_out, not_1_out, not_2_out, not_3_out, x[4], not_5_out, not_6_out, not_7_out, x[0]);
  and and_13 (and_13_out, x[7], not_2_out, not_3_out, x[4], not_5_out, not_6_out, x[1], not_8_out);
  and and_14 (and_14_out, not_1_out, not_2_out, not_3_out, x[4], not_5_out, x[2], not_7_out, not_8_out);
  and and_15 (and_15_out, x[7], not_2_out, not_3_out, x[4], not_5_out, x[2], not_7_out, x[0]);
  and and_16 (and_16_out, not_1_out, not_2_out, not_3_out, x[4], not_5_out, x[2], x[1], x[0]);
  and and_17 (and_17_out, x[7], not_2_out, not_3_out, x[4], x[3], not_6_out, not_7_out, not_8_out);
  and and_18 (and_18_out, not_1_out, not_2_out, not_3_out, x[4], x[3], not_6_out, x[1], not_8_out);
  and and_19 (and_19_out, x[7], not_2_out, not_3_out, x[4], x[3], not_6_out, x[1], x[0]);
  and and_20 (and_20_out, not_1_out, not_2_out, not_3_out, x[4], x[3], x[2], not_7_out, x[0]);
  and and_21 (and_21_out, x[7], not_2_out, not_3_out, x[4], x[3], x[2], x[1], not_8_out);
  and and_22 (and_22_out, not_1_out, not_2_out, x[5], not_4_out, not_5_out, not_6_out, not_7_out, not_8_out);
  and and_23 (and_23_out, x[7], not_2_out, x[5], not_4_out, not_5_out, not_6_out, not_7_out, x[0]);
  and and_24 (and_24_out, not_1_out, not_2_out, x[5], not_4_out, not_5_out, not_6_out, x[1], x[0]);
  and and_25 (and_25_out, x[7], not_2_out, x[5], not_4_out, not_5_out, x[2], not_7_out, not_8_out);
  and and_26 (and_26_out, not_1_out, not_2_out, x[5], not_4_out, not_5_out, x[2], x[1], not_8_out);
  and and_27 (and_27_out, x[7], not_2_out, x[5], not_4_out, not_5_out, x[2], x[1], x[0]);
  and and_28 (and_28_out, not_1_out, not_2_out, x[5], not_4_out, x[3], not_6_out, not_7_out, x[0]);
  and and_29 (and_29_out, x[7], not_2_out, x[5], not_4_out, x[3], not_6_out, x[1], not_8_out);
  and and_30 (and_30_out, not_1_out, not_2_out, x[5], not_4_out, x[3], x[2], not_7_out, not_8_out);
  and and_31 (and_31_out, x[7], not_2_out, x[5], not_4_out, x[3], x[2], not_7_out, x[0]);
  and and_32 (and_32_out, not_1_out, not_2_out, x[5], not_4_out, x[3], x[2], x[1], x[0]);
  and and_33 (and_33_out, x[7], not_2_out, x[5], x[4], not_5_out, not_6_out, not_7_out, not_8_out);
  and and_34 (and_34_out, not_1_out, not_2_out, x[5], x[4], not_5_out, not_6_out, x[1], not_8_out);
  and and_35 (and_35_out, x[7], not_2_out, x[5], x[4], not_5_out, not_6_out, x[1], x[0]);
  and and_36 (and_36_out, not_1_out, not_2_out, x[5], x[4], not_5_out, x[2], not_7_out, x[0]);
  and and_37 (and_37_out, x[7], not_2_out, x[5], x[4], not_5_out, x[2], x[1], not_8_out);
  and and_38 (and_38_out, not_1_out, not_2_out, x[5], x[4], x[3], not_6_out, not_7_out, not_8_out);
  and and_39 (and_39_out, x[7], not_2_out, x[5], x[4], x[3], not_6_out, not_7_out, x[0]);
  and and_40 (and_40_out, not_1_out, not_2_out, x[5], x[4], x[3], not_6_out, x[1], x[0]);
  and and_41 (and_41_out, x[7], not_2_out, x[5], x[4], x[3], x[2], not_7_out, not_8_out);
  and and_42 (and_42_out, not_1_out, not_2_out, x[5], x[4], x[3], x[2], x[1], not_8_out);
  and and_43 (and_43_out, x[7], not_2_out, x[5], x[4], x[3], x[2], x[1], x[0]);
  and and_44 (and_44_out, not_1_out, x[6], not_3_out, not_4_out, not_5_out, not_6_out, not_7_out, x[0]);
  and and_45 (and_45_out, x[7], x[6], not_3_out, not_4_out, not_5_out, not_6_out, x[1], not_8_out);
  and and_46 (and_46_out, not_1_out, x[6], not_3_out, not_4_out, not_5_out, x[2], not_7_out, not_8_out);
  and and_47 (and_47_out, x[7], x[6], not_3_out, not_4_out, not_5_out, x[2], not_7_out, x[0]);
  and and_48 (and_48_out, not_1_out, x[6], not_3_out, not_4_out, not_5_out, x[2], x[1], x[0]);
  and and_49 (and_49_out, x[7], x[6], not_3_out, not_4_out, x[3], not_6_out, not_7_out, not_8_out);
  and and_50 (and_50_out, not_1_out, x[6], not_3_out, not_4_out, x[3], not_6_out, x[1], not_8_out);
  and and_51 (and_51_out, x[7], x[6], not_3_out, not_4_out, x[3], not_6_out, x[1], x[0]);
  and and_52 (and_52_out, not_1_out, x[6], not_3_out, not_4_out, x[3], x[2], not_7_out, x[0]);
  and and_53 (and_53_out, x[7], x[6], not_3_out, not_4_out, x[3], x[2], x[1], not_8_out);
  and and_54 (and_54_out, not_1_out, x[6], not_3_out, x[4], not_5_out, not_6_out, not_7_out, not_8_out);
  and and_55 (and_55_out, x[7], x[6], not_3_out, x[4], not_5_out, not_6_out, not_7_out, x[0]);
  and and_56 (and_56_out, not_1_out, x[6], not_3_out, x[4], not_5_out, not_6_out, x[1], x[0]);
  and and_57 (and_57_out, x[7], x[6], not_3_out, x[4], not_5_out, x[2], not_7_out, not_8_out);
  and and_58 (and_58_out, not_1_out, x[6], not_3_out, x[4], not_5_out, x[2], x[1], not_8_out);
  and and_59 (and_59_out, x[7], x[6], not_3_out, x[4], not_5_out, x[2], x[1], x[0]);
  and and_60 (and_60_out, not_1_out, x[6], not_3_out, x[4], x[3], not_6_out, not_7_out, x[0]);
  and and_61 (and_61_out, x[7], x[6], not_3_out, x[4], x[3], not_6_out, x[1], not_8_out);
  and and_62 (and_62_out, not_1_out, x[6], not_3_out, x[4], x[3], x[2], not_7_out, not_8_out);
  and and_63 (and_63_out, x[7], x[6], not_3_out, x[4], x[3], x[2], not_7_out, x[0]);
  and and_64 (and_64_out, not_1_out, x[6], not_3_out, x[4], x[3], x[2], x[1], x[0]);
  and and_65 (and_65_out, x[7], x[6], x[5], not_4_out, not_5_out, not_6_out, not_7_out, not_8_out);
  and and_66 (and_66_out, not_1_out, x[6], x[5], not_4_out, not_5_out, not_6_out, x[1], not_8_out);
  and and_67 (and_67_out, x[7], x[6], x[5], not_4_out, not_5_out, not_6_out, x[1], x[0]);
  and and_68 (and_68_out, not_1_out, x[6], x[5], not_4_out, not_5_out, x[2], not_7_out, x[0]);
  and and_69 (and_69_out, x[7], x[6], x[5], not_4_out, not_5_out, x[2], x[1], not_8_out);
  and and_70 (and_70_out, not_1_out, x[6], x[5], not_4_out, x[3], not_6_out, not_7_out, not_8_out);
  and and_71 (and_71_out, x[7], x[6], x[5], not_4_out, x[3], not_6_out, not_7_out, x[0]);
  and and_72 (and_72_out, not_1_out, x[6], x[5], not_4_out, x[3], not_6_out, x[1], x[0]);
  and and_73 (and_73_out, x[7], x[6], x[5], not_4_out, x[3], x[2], not_7_out, not_8_out);
  and and_74 (and_74_out, not_1_out, x[6], x[5], not_4_out, x[3], x[2], x[1], not_8_out);
  and and_75 (and_75_out, x[7], x[6], x[5], not_4_out, x[3], x[2], x[1], x[0]);
  and and_76 (and_76_out, not_1_out, x[6], x[5], x[4], not_5_out, not_6_out, not_7_out, x[0]);
  and and_77 (and_77_out, x[7], x[6], x[5], x[4], not_5_out, not_6_out, x[1], not_8_out);
  and and_78 (and_78_out, not_1_out, x[6], x[5], x[4], not_5_out, x[2], not_7_out, not_8_out);
  and and_79 (and_79_out, x[7], x[6], x[5], x[4], not_5_out, x[2], not_7_out, x[0]);
  and and_80 (and_80_out, not_1_out, x[6], x[5], x[4], not_5_out, x[2], x[1], x[0]);
  and and_81 (and_81_out, x[7], x[6], x[5], x[4], x[3], not_6_out, not_7_out, not_8_out);
  and and_82 (and_82_out, not_1_out, x[6], x[5], x[4], x[3], not_6_out, x[1], not_8_out);
  and and_83 (and_83_out, x[7], x[6], x[5], x[4], x[3], not_6_out, x[1], x[0]);
  and and_84 (and_84_out, not_1_out, x[6], x[5], x[4], x[3], x[2], not_7_out, x[0]);
  and and_85 (and_85_out, x[7], x[6], x[5], x[4], x[3], x[2], x[1], not_8_out);
  and and_86 (and_86_out, not_1_out, not_2_out, not_3_out, not_4_out, not_5_out, not_6_out, not_7_out, x[0]);
  and and_87 (and_87_out, x[7], not_2_out, not_3_out, not_4_out, not_5_out, not_6_out, x[1], not_8_out);
  and and_88 (and_88_out, not_1_out, not_2_out, not_3_out, not_4_out, not_5_out, x[2], not_7_out, not_8_out);
  and and_89 (and_89_out, x[7], not_2_out, not_3_out, not_4_out, not_5_out, x[2], not_7_out, x[0]);
  and and_90 (and_90_out, not_1_out, not_2_out, not_3_out, not_4_out, not_5_out, x[2], x[1], x[0]);
  and and_91 (and_91_out, x[7], not_2_out, not_3_out, not_4_out, x[3], not_6_out, not_7_out, not_8_out);
  and and_92 (and_92_out, not_1_out, not_2_out, not_3_out, not_4_out, x[3], not_6_out, x[1], not_8_out);
  and and_93 (and_93_out, x[7], not_2_out, not_3_out, not_4_out, x[3], not_6_out, x[1], x[0]);
  and and_94 (and_94_out, not_1_out, not_2_out, not_3_out, not_4_out, x[3], x[2], not_7_out, x[0]);
  and and_95 (and_95_out, x[7], not_2_out, not_3_out, not_4_out, x[3], x[2], x[1], not_8_out);
  and and_96 (and_96_out, not_1_out, not_2_out, not_3_out, x[4], not_5_out, not_6_out, not_7_out, not_8_out);
  and and_97 (and_97_out, x[7], not_2_out, not_3_out, x[4], not_5_out, not_6_out, not_7_out, x[0]);
  and and_98 (and_98_out, not_1_out, not_2_out, not_3_out, x[4], not_5_out, not_6_out, x[1], x[0]);
  and and_99 (and_99_out, x[7], not_2_out, not_3_out, x[4], not_5_out, x[2], not_7_out, not_8_out);
  and and_100 (and_100_out, not_1_out, not_2_out, not_3_out, x[4], not_5_out, x[2], x[1], not_8_out);
  and and_101 (and_101_out, x[7], not_2_out, not_3_out, x[4], not_5_out, x[2], x[1], x[0]);
  and and_102 (and_102_out, not_1_out, not_2_out, not_3_out, x[4], x[3], not_6_out, not_7_out, x[0]);
  and and_103 (and_103_out, x[7], not_2_out, not_3_out, x[4], x[3], not_6_out, x[1], not_8_out);
  and and_104 (and_104_out, not_1_out, not_2_out, not_3_out, x[4], x[3], x[2], not_7_out, not_8_out);
  and and_105 (and_105_out, x[7], not_2_out, not_3_out, x[4], x[3], x[2], not_7_out, x[0]);
  and and_106 (and_106_out, not_1_out, not_2_out, not_3_out, x[4], x[3], x[2], x[1], x[0]);
  and and_107 (and_107_out, x[7], not_2_out, x[5], not_4_out, not_5_out, not_6_out, not_7_out, not_8_out);
  and and_108 (and_108_out, not_1_out, not_2_out, x[5], not_4_out, not_5_out, not_6_out, x[1], not_8_out);
  and and_109 (and_109_out, x[7], not_2_out, x[5], not_4_out, not_5_out, not_6_out, x[1], x[0]);
  and and_110 (and_110_out, not_1_out, not_2_out, x[5], not_4_out, not_5_out, x[2], not_7_out, x[0]);
  and and_111 (and_111_out, x[7], not_2_out, x[5], not_4_out, not_5_out, x[2], x[1], not_8_out);
  and and_112 (and_112_out, not_1_out, not_2_out, x[5], not_4_out, x[3], not_6_out, not_7_out, not_8_out);
  and and_113 (and_113_out, x[7], not_2_out, x[5], not_4_out, x[3], not_6_out, not_7_out, x[0]);
  and and_114 (and_114_out, not_1_out, not_2_out, x[5], not_4_out, x[3], not_6_out, x[1], x[0]);
  and and_115 (and_115_out, x[7], not_2_out, x[5], not_4_out, x[3], x[2], not_7_out, not_8_out);
  and and_116 (and_116_out, not_1_out, not_2_out, x[5], not_4_out, x[3], x[2], x[1], not_8_out);
  and and_117 (and_117_out, x[7], not_2_out, x[5], not_4_out, x[3], x[2], x[1], x[0]);
  and and_118 (and_118_out, not_1_out, not_2_out, x[5], x[4], not_5_out, not_6_out, not_7_out, x[0]);
  and and_119 (and_119_out, x[7], not_2_out, x[5], x[4], not_5_out, not_6_out, x[1], not_8_out);
  and and_120 (and_120_out, not_1_out, not_2_out, x[5], x[4], not_5_out, x[2], not_7_out, not_8_out);
  and and_121 (and_121_out, x[7], not_2_out, x[5], x[4], not_5_out, x[2], not_7_out, x[0]);
  and and_122 (and_122_out, not_1_out, not_2_out, x[5], x[4], not_5_out, x[2], x[1], x[0]);
  and and_123 (and_123_out, x[7], not_2_out, x[5], x[4], x[3], not_6_out, not_7_out, not_8_out);
  and and_124 (and_124_out, not_1_out, not_2_out, x[5], x[4], x[3], not_6_out, x[1], not_8_out);
  and and_125 (and_125_out, x[7], not_2_out, x[5], x[4], x[3], not_6_out, x[1], x[0]);
  and and_126 (and_126_out, not_1_out, not_2_out, x[5], x[4], x[3], x[2], not_7_out, x[0]);
  and and_127 (and_127_out, x[7], not_2_out, x[5], x[4], x[3], x[2], x[1], not_8_out);
  and and_128 (and_128_out, not_1_out, x[6], not_3_out, not_4_out, not_5_out, not_6_out, not_7_out, not_8_out);
  and and_129 (and_129_out, x[7], x[6], not_3_out, not_4_out, not_5_out, not_6_out, not_7_out, x[0]);
  and and_130 (and_130_out, not_1_out, x[6], not_3_out, not_4_out, not_5_out, not_6_out, x[1], x[0]);
  and and_131 (and_131_out, x[7], x[6], not_3_out, not_4_out, not_5_out, x[2], not_7_out, not_8_out);
  and and_132 (and_132_out, not_1_out, x[6], not_3_out, not_4_out, not_5_out, x[2], x[1], not_8_out);
  and and_133 (and_133_out, x[7], x[6], not_3_out, not_4_out, not_5_out, x[2], x[1], x[0]);
  and and_134 (and_134_out, not_1_out, x[6], not_3_out, not_4_out, x[3], not_6_out, not_7_out, x[0]);
  and and_135 (and_135_out, x[7], x[6], not_3_out, not_4_out, x[3], not_6_out, x[1], not_8_out);
  and and_136 (and_136_out, not_1_out, x[6], not_3_out, not_4_out, x[3], x[2], not_7_out, not_8_out);
  and and_137 (and_137_out, x[7], x[6], not_3_out, not_4_out, x[3], x[2], not_7_out, x[0]);
  and and_138 (and_138_out, not_1_out, x[6], not_3_out, not_4_out, x[3], x[2], x[1], x[0]);
  and and_139 (and_139_out, x[7], x[6], not_3_out, x[4], not_5_out, not_6_out, not_7_out, not_8_out);
  and and_140 (and_140_out, not_1_out, x[6], not_3_out, x[4], not_5_out, not_6_out, x[1], not_8_out);
  and and_141 (and_141_out, x[7], x[6], not_3_out, x[4], not_5_out, not_6_out, x[1], x[0]);
  and and_142 (and_142_out, not_1_out, x[6], not_3_out, x[4], not_5_out, x[2], not_7_out, x[0]);
  and and_143 (and_143_out, x[7], x[6], not_3_out, x[4], not_5_out, x[2], x[1], not_8_out);
  and and_144 (and_144_out, not_1_out, x[6], not_3_out, x[4], x[3], not_6_out, not_7_out, not_8_out);
  and and_145 (and_145_out, x[7], x[6], not_3_out, x[4], x[3], not_6_out, not_7_out, x[0]);
  and and_146 (and_146_out, not_1_out, x[6], not_3_out, x[4], x[3], not_6_out, x[1], x[0]);
  and and_147 (and_147_out, x[7], x[6], not_3_out, x[4], x[3], x[2], not_7_out, not_8_out);
  and and_148 (and_148_out, not_1_out, x[6], not_3_out, x[4], x[3], x[2], x[1], not_8_out);
  and and_149 (and_149_out, x[7], x[6], not_3_out, x[4], x[3], x[2], x[1], x[0]);
  and and_150 (and_150_out, not_1_out, x[6], x[5], not_4_out, not_5_out, not_6_out, not_7_out, x[0]);
  and and_151 (and_151_out, x[7], x[6], x[5], not_4_out, not_5_out, not_6_out, x[1], not_8_out);
  and and_152 (and_152_out, not_1_out, x[6], x[5], not_4_out, not_5_out, x[2], not_7_out, not_8_out);
  and and_153 (and_153_out, x[7], x[6], x[5], not_4_out, not_5_out, x[2], not_7_out, x[0]);
  and and_154 (and_154_out, not_1_out, x[6], x[5], not_4_out, not_5_out, x[2], x[1], x[0]);
  and and_155 (and_155_out, x[7], x[6], x[5], not_4_out, x[3], not_6_out, not_7_out, not_8_out);
  and and_156 (and_156_out, not_1_out, x[6], x[5], not_4_out, x[3], not_6_out, x[1], not_8_out);
  and and_157 (and_157_out, x[7], x[6], x[5], not_4_out, x[3], not_6_out, x[1], x[0]);
  and and_158 (and_158_out, not_1_out, x[6], x[5], not_4_out, x[3], x[2], not_7_out, x[0]);
  and and_159 (and_159_out, x[7], x[6], x[5], not_4_out, x[3], x[2], x[1], not_8_out);
  and and_160 (and_160_out, not_1_out, x[6], x[5], x[4], not_5_out, not_6_out, not_7_out, not_8_out);
  and and_161 (and_161_out, x[7], x[6], x[5], x[4], not_5_out, not_6_out, not_7_out, x[0]);
  and and_162 (and_162_out, not_1_out, x[6], x[5], x[4], not_5_out, not_6_out, x[1], x[0]);
  and and_163 (and_163_out, x[7], x[6], x[5], x[4], not_5_out, x[2], not_7_out, not_8_out);
  and and_164 (and_164_out, not_1_out, x[6], x[5], x[4], not_5_out, x[2], x[1], not_8_out);
  and and_165 (and_165_out, x[7], x[6], x[5], x[4], not_5_out, x[2], x[1], x[0]);
  and and_166 (and_166_out, not_1_out, x[6], x[5], x[4], x[3], not_6_out, not_7_out, x[0]);
  and and_167 (and_167_out, x[7], x[6], x[5], x[4], x[3], not_6_out, x[1], not_8_out);
  and and_168 (and_168_out, not_1_out, x[6], x[5], x[4], x[3], x[2], not_7_out, not_8_out);
  and and_169 (and_169_out, x[7], x[6], x[5], x[4], x[3], x[2], not_7_out, x[0]);
  and and_170 (and_170_out, not_1_out, x[6], x[5], x[4], x[3], x[2], x[1], x[0]);
  or or_1 (or_1_out, and_1_out, and_2_out, and_3_out, and_4_out, and_5_out, and_6_out, and_7_out, and_8_out, and_9_out, and_10_out, and_11_out, and_12_out, and_13_out, and_14_out, and_15_out, and_16_out, and_17_out, and_18_out, and_19_out, and_20_out, and_21_out, and_22_out, and_23_out, and_24_out, and_25_out, and_26_out, and_27_out, and_28_out, and_29_out, and_30_out, and_31_out, and_32_out, and_33_out, and_34_out, and_35_out, and_36_out, and_37_out, and_38_out, and_39_out, and_40_out, and_41_out, and_42_out, and_43_out);
  or or_2 (or_2_out, and_44_out, and_45_out, and_46_out, and_47_out, and_48_out, and_49_out, and_50_out, and_51_out, and_52_out, and_53_out, and_54_out, and_55_out, and_56_out, and_57_out, and_58_out, and_59_out, and_60_out, and_61_out, and_62_out, and_63_out, and_64_out, and_65_out, and_66_out, and_67_out, and_68_out, and_69_out, and_70_out, and_71_out, and_72_out, and_73_out, and_74_out, and_75_out, and_76_out, and_77_out, and_78_out, and_79_out, and_80_out, and_81_out, and_82_out, and_83_out, and_84_out, and_85_out);
  or or_3 (or_3_out, and_86_out, and_87_out, and_88_out, and_89_out, and_90_out, and_91_out, and_92_out, and_93_out, and_94_out, and_95_out, and_96_out, and_97_out, and_98_out, and_99_out, and_100_out, and_101_out, and_102_out, and_103_out, and_104_out, and_105_out, and_106_out, and_107_out, and_108_out, and_109_out, and_110_out, and_111_out, and_112_out, and_113_out, and_114_out, and_115_out, and_116_out, and_117_out, and_118_out, and_119_out, and_120_out, and_121_out, and_122_out, and_123_out, and_124_out, and_125_out, and_126_out, and_127_out, and_128_out);
  or or_4 (or_4_out, and_129_out, and_130_out, and_131_out, and_132_out, and_133_out, and_134_out, and_135_out, and_136_out, and_137_out, and_138_out, and_139_out, and_140_out, and_141_out, and_142_out, and_143_out, and_144_out, and_145_out, and_146_out, and_147_out, and_148_out, and_149_out, and_150_out, and_151_out, and_152_out, and_153_out, and_154_out, and_155_out, and_156_out, and_157_out, and_158_out, and_159_out, and_160_out, and_161_out, and_162_out, and_163_out, and_164_out, and_165_out, and_166_out, and_167_out, and_168_out, and_169_out, and_170_out);
  or or_5 (y[1], or_1_out, or_2_out);
  or or_6 (y[0], or_3_out, or_4_out);
endmodule

module thesame2x2 (
  input  [1:0] a,
  input  [1:0] b,
  output ok
);

  wire and_1_out, and_2_out, and_3_out, and_4_out, not_1_out, not_2_out, not_3_out, not_4_out;

  not not_1 (not_1_out, a[1]);
  not not_2 (not_2_out, a[0]);
  not not_3 (not_3_out, b[1]);
  not not_4 (not_4_out, b[0]);
  and and_1 (and_1_out, not_1_out, not_2_out, not_3_out, not_4_out);
  and and_2 (and_2_out, not_1_out, a[0], not_3_out, b[0]);
  and and_3 (and_3_out, a[1], not_2_out, b[1], not_4_out);
  and and_4 (and_4_out, a[1], a[0], b[1], b[0]);
  or or_1 (ok, and_1_out, and_2_out, and_3_out, and_4_out);
endmodule
